# Fritzing sketch PS2-USB (saved by Fritzing 0.7.4b)
breadboards: 1

parts:
  R1 = Resistor [tolerance=±5% resistance=10k package=THT]
  R2 = Resistor [tolerance=±5% resistance=5.6k package=THT]
  J1 = female pin header, 9 pins [form="♀ (female)"]
  R3 = Resistor [tolerance=±5% resistance=5.6k package=THT]
  Teensy = Teensy 2.0

nets:
  5V: R1.Pin_0, J1.pin5, Teensy.VCC
  N1: R1.Pin_1, J1.pin1, Teensy.B3
  N2: R2.Pin_0, Teensy.B2
  N3: R2.Pin_1, J1.pin6
  N4: J1.pin2, Teensy.B1
  GND: J1.pin4, Teensy.GND
  N5: J1.pin7, R3.Pin_1
  N6: R3.Pin_0, Teensy.B0

notes:
  PS2 Controller to USB Converter, PS2-USB, 1
  Made by Duncan Murdock
  PS2-USB
